# Fritzing sketch Cuboid_v1 (saved by Fritzing 0.9.3b)
breadboards: 1

parts:
  Part1 = Arduino Mega 2560 (Rev3)
  WeMos_D1_Mini_Relay_Shield1 = WeMos D1 Mini Relay Shield
  WeMos_D1_Mini_Relay_Shield2 = WeMos D1 Mini Relay Shield
  WeMos_D1_Mini_Relay_Shield3 = WeMos D1 Mini Relay Shield
  WeMos_D1_Mini_Relay_Shield4 = WeMos D1 Mini Relay Shield
  WeMos_D1_Mini_Relay_Shield5 = WeMos D1 Mini Relay Shield
  L2 = Solenoid  # not connected
  L3 = Solenoid  # not connected
  L4 = Solenoid  # not connected
  L5 = Solenoid  # not connected
  L6 = Solenoid  # not connected
  Part2 = IMU Digital Combo Board 6DOF

nets:
  N1: Part1.D21/SCL, Part2.SCL
  N2: Part1.D20/SDA, Part2.SDA
  3V3: Part1.3V3, Part2.3.3V
  5V: Part1.5V, WeMos_D1_Mini_Relay_Shield1.5V, WeMos_D1_Mini_Relay_Shield2.5V, WeMos_D1_Mini_Relay_Shield3.5V, WeMos_D1_Mini_Relay_Shield4.5V, WeMos_D1_Mini_Relay_Shield5.5V
  GND: Part1.GND, WeMos_D1_Mini_Relay_Shield1.G, WeMos_D1_Mini_Relay_Shield2.G, WeMos_D1_Mini_Relay_Shield3.G, WeMos_D1_Mini_Relay_Shield4.G, WeMos_D1_Mini_Relay_Shield5.G, Part2.GND
  N3: Part1.D2_PWM, WeMos_D1_Mini_Relay_Shield3.D1
  N4: Part1.D3_PWM, WeMos_D1_Mini_Relay_Shield4.D1
  N5: Part1.D4_PWM, WeMos_D1_Mini_Relay_Shield2.D1
  N6: Part1.D5_PWM, WeMos_D1_Mini_Relay_Shield1.D1
  N7: Part1.D6_PWM, WeMos_D1_Mini_Relay_Shield5.D1
